# Fritzing sketch GAMEPAD (saved by Fritzing 0.9.0b)
circuit board: 8.73728cm x 4.00487cm

parts:
  Pro_Micro1 = SparkFun Pro Micro
  S1 = Pushbutton [package="[THT]"]
  S2 = Pushbutton [package="[THT]"]
  S3 = Pushbutton [package="[THT]"]
  S4 = Pushbutton [package="[THT]"]
  S5 = Pushbutton [package="[THT]"]
  S6 = Pushbutton [package="[THT]"]
  S7 = Pushbutton [package="[THT]"]
  S8 = Pushbutton [package="[THT]"]
  S9 = Pushbutton [package="[THT]"]
  S10 = Pushbutton [package="[THT]"]

nets:
  N1: Pro_Micro1.GND, S1.Pin_3, S2.Pin_3, S2.Pin_4, S3.Pin_3, S3.Pin_4, S4.Pin_3, S4.Pin_4, S5.Pin_3, S5.Pin_4, S6.Pin_3, S6.Pin_4, S7.Pin_3, S7.Pin_4, S8.Pin_3, S8.Pin_4, S9.Pin_3, S9.Pin_4, S10.Pin_4
  N2: Pro_Micro1.2, S2.Pin_1
  N3: Pro_Micro1.3, S3.Pin_1, S3.Pin_2
  N4: Pro_Micro1.4, S4.Pin_1
  N5: Pro_Micro1.5, S1.Pin_1, S1.Pin_2
  N6: Pro_Micro1.8, S9.Pin_1, S9.Pin_2
  N7: Pro_Micro1.9, S10.Pin_1, S10.Pin_2
  N8: Pro_Micro1.10, S7.Pin_2
  N9: Pro_Micro1.16, S8.Pin_2
  N10: Pro_Micro1.14, S6.Pin_2
  N11: Pro_Micro1.15, S5.Pin_1, S5.Pin_2

custom parts:
  SparkFun Pro Micro: The Pro Micro is similar to the Pro Mini except with an ATmega32U4 on board. The USB transceiver inside the 32U4 allows us to add USB connectivity on-board and do away with bulky external USB interface. Based on: https://github.com/unorthodox-engineers/unorthodox-arduino/blob/master/Unorthodox/fritzing/parts/Pro%20Micro.fzpz
